// Logisim project lg.circ as structural Verilog: 1 circuit, main circuit main
module main (
  input  S5,
  input  S4,
  input  S3,
  input  S2,
  input  S1,
  input  S0,
  output M,
  output F,
  output I,
  output B2,
  output J,
  output B1,
  output R
);

  wire and_2_out, and_3_out, and_4_out, and_5_out, and_6_out, and_7_out, and_8_out, and_9_out, and_12_out,
       and_13_out, and_14_out, and_15_out, and_16_out, and_17_out, not_1_out, not_2_out, not_3_out,
       not_4_out, not_5_out, not_6_out;

  not not_1 (not_1_out, S1);
  not not_2 (not_2_out, S2);
  not not_3 (not_3_out, S5);
  not not_4 (not_4_out, S4);
  not not_5 (not_5_out, S3);
  not not_6 (not_6_out, S0);
  and and_1 (F, not_3_out, S4);
  and and_2 (and_2_out, not_3_out, not_4_out);
  and and_3 (and_3_out, not_3_out, not_4_out);
  and and_4 (and_4_out, not_5_out, S2);
  and and_5 (and_5_out, not_3_out, not_4_out);
  and and_6 (and_6_out, not_3_out, not_4_out);
  and and_7 (and_7_out, not_2_out, not_1_out);
  and and_8 (and_8_out, not_3_out, not_4_out);
  and and_9 (and_9_out, not_2_out, not_1_out);
  and and_10 (I, and_2_out, S3);
  and and_11 (B2, and_3_out, and_4_out);
  and and_12 (and_12_out, and_5_out, not_5_out);
  and and_13 (and_13_out, not_2_out, S1);
  and and_14 (and_14_out, and_6_out, not_5_out);
  and and_15 (and_15_out, and_7_out, S0);
  and and_16 (and_16_out, and_8_out, not_5_out);
  and and_17 (and_17_out, and_9_out, not_6_out);
  and and_18 (J, and_12_out, and_13_out);
  and and_19 (B1, and_14_out, and_15_out);
  and and_20 (R, and_16_out, and_17_out);

  assign M = S5;
endmodule
