// Logisim project lga.circ as structural Verilog: 2 circuits, main circuit main
module main (
  input  S5,
  input  S4,
  input  S3,
  input  S2,
  input  S1,
  input  S0,
  output R,
  output B1,
  output J,
  output B2,
  output I,
  output F,
  output M
);

  wire not_1_out, not_2_out, not_3_out, not_4_out, not_5_out, not_6_out, not_7_out, not_8_out, not_9_out,
       not_10_out, not_11_out, not_12_out, not_13_out, not_14_out, not_15_out, not_16_out, not_17_out,
       not_18_out, not_19_out, not_20_out, not_21_out;

  not not_1 (not_1_out, S5);
  not not_2 (not_2_out, S4);
  not not_3 (not_3_out, S3);
  not not_4 (not_4_out, S2);
  not not_5 (not_5_out, S1);
  not not_6 (not_6_out, S0);
  not not_7 (not_7_out, S5);
  not not_8 (not_8_out, S4);
  not not_9 (not_9_out, S3);
  not not_10 (not_10_out, S2);
  not not_11 (not_11_out, S1);
  not not_12 (not_12_out, S5);
  not not_13 (not_13_out, S4);
  not not_14 (not_14_out, S3);
  not not_15 (not_15_out, S2);
  not not_16 (not_16_out, S5);
  not not_17 (not_17_out, S4);
  not not_18 (not_18_out, S3);
  not not_19 (not_19_out, S5);
  not not_20 (not_20_out, S4);
  not not_21 (not_21_out, S5);
  and and_1 (R, not_1_out, not_2_out, not_3_out, not_4_out, not_5_out, not_6_out);
  and and_2 (B1, not_7_out, not_8_out, not_9_out, not_10_out, not_11_out, S0);
  and and_3 (J, not_12_out, not_13_out, not_14_out, not_15_out, S1);
  and and_4 (B2, not_16_out, not_17_out, not_18_out, S2);
  and and_5 (I, not_19_out, not_20_out, S3);
  and and_6 (F, not_21_out, S4);

  assign M = S5;
endmodule

module ll (
  input  S5,
  input  S4,
  input  S3,
  input  S2,
  input  S1,
  input  S0,
  output R,
  output B1,
  output J,
  output B2,
  output I,
  output F,
  output M
);

  wire and_1_out, and_2_out, and_3_out, and_4_out, and_5_out, and_6_out, and_7_out, and_8_out, and_10_out,
       and_11_out, and_12_out, and_13_out, and_14_out, and_15_out, not_1_out, not_2_out, not_3_out,
       not_4_out, not_5_out, not_6_out;

  not not_1 (not_1_out, S5);
  not not_2 (not_2_out, S4);
  not not_3 (not_3_out, S3);
  not not_4 (not_4_out, S2);
  not not_5 (not_5_out, S1);
  not not_6 (not_6_out, S0);
  and and_1 (and_1_out, not_1_out, not_2_out);
  and and_2 (and_2_out, not_4_out, not_5_out);
  and and_3 (and_3_out, not_1_out, not_2_out);
  and and_4 (and_4_out, not_4_out, not_5_out);
  and and_5 (and_5_out, not_1_out, not_2_out);
  and and_6 (and_6_out, not_1_out, not_2_out);
  and and_7 (and_7_out, not_3_out, S2);
  and and_8 (and_8_out, not_1_out, not_2_out);
  and and_9 (F, not_1_out, S4);
  and and_10 (and_10_out, and_1_out, not_3_out);
  and and_11 (and_11_out, and_2_out, not_6_out);
  and and_12 (and_12_out, and_3_out, not_3_out);
  and and_13 (and_13_out, and_4_out, S0);
  and and_14 (and_14_out, and_5_out, not_3_out);
  and and_15 (and_15_out, not_4_out, S1);
  and and_16 (B2, and_6_out, and_7_out);
  and and_17 (I, and_8_out, S3);
  and and_18 (R, and_10_out, and_11_out);
  and and_19 (B1, and_12_out, and_13_out);
  and and_20 (J, and_14_out, and_15_out);

  assign M = S5;
endmodule
